// Logisim project Ejercicio2.circ as structural Verilog: 2 circuits, main circuit main
module main (
  input  [2:0] ABC,
  input  [2:0] DEF,
  input  [2:0] GHI
);

  wire Procesar_out;

  Button Procesar (.out(Procesar_out));
endmodule

module Memoria_Interna (
  input  in_1,
  input  [2:0] in_2
);

  wire decoder_1_out0, decoder_1_out1, decoder_1_out2, decoder_1_out3, decoder_1_out4, decoder_1_out5,
       decoder_1_out6, decoder_1_out7;

  Decoder #(.select(3)) decoder_1 (
    .out0(decoder_1_out0), .out1(decoder_1_out1), .out2(decoder_1_out2), .out3(decoder_1_out3),
    .out4(decoder_1_out4), .out5(decoder_1_out5), .out6(decoder_1_out6), .out7(decoder_1_out7), .sel(in_2),
    .en(in_1));
endmodule
